// Logisim project Tris.circ as structural Verilog: 2 circuits, main circuit base
module base (
);

  wire b1, b2, b3, b4, b5, b6, b7, b8, b9, clock_1_out, r1, r2, r3, r4, r5, r6, r7, r8, r9;
  wire [7:0] counter_1_q, rom_1_data;

  Counter #(.max('h8)) counter_1 (
    .Q(counter_1_q), .clk(clock_1_out));  // open: load, D, count, carry, clr, preset, down
  Clock clock_1 (.out(clock_1_out));
  // ß2018 ß2018_1: pin names not known
  ROM #(.Select("low")) rom_1 (.addr(counter_1_q), .data(rom_1_data));
  Demultiplexer #(.select(4), .width(2), .enable("false")) demultiplexer_1 (
    .out0({b1, r1}), .out1({b2, r2}), .out2({b3, r3}), .out3({b4, r4}), .out4({b5, r5}), .out5({b6, r6}),
    .out6({b7, r7}), .out7({b8, r8}), .out8({b9, r9}), .in(rom_1_data[1:0]), .sel(counter_1_q[3:0]));  // open: out9, out10, out11, out12, out13, out14, out15
  // RGBLed rgbled_1: pin names not known; wires that end beside it: r1, b1
  // RGBLed rgbled_2: pin names not known; wires that end beside it: r4, b4
  // RGBLed rgbled_3: pin names not known; wires that end beside it: r7, b7
  // RGBLed rgbled_4: pin names not known; wires that end beside it: r3, b3
  // RGBLed rgbled_5: pin names not known; wires that end beside it: r2, b2
  // RGBLed rgbled_6: pin names not known; wires that end beside it: r6, b6
  // RGBLed rgbled_7: pin names not known; wires that end beside it: r5, b5
  // RGBLed rgbled_8: pin names not known; wires that end beside it: r8, b8
  // RGBLed rgbled_9: pin names not known; wires that end beside it: r9, b9

  // Notes on the sheet:
  //   contents of rom_1 (hex, n*v repeats v):
  //   1 2 2 1 3 1 2 2 3
endmodule

module test (
);

  wire _1, _2, _3, _4, _5, _6, _7, _8, _9, b1, b2, b3, b4, b5, b6, b7, b8, b9, clk, CONFIRM_out, r1, r2, r3,
       r4, r5, r6, r7, r8, r9;
  wire [1:0] adder_1_out, counter_1_q, demultiplexer_1_out0, demultiplexer_1_out1, demultiplexer_1_out2,
       demultiplexer_1_out3, demultiplexer_1_out4, demultiplexer_1_out5, demultiplexer_1_out6,
       demultiplexer_1_out7, demultiplexer_1_out8, ram_1_data;
  wire [3:0] counter_2_q;

  // RGBLed rgbled_1: pin names not known; wires that end beside it: r1, _1, b1
  // RGBLed rgbled_2: pin names not known; wires that end beside it: r4, _4, b4
  // RGBLed rgbled_3: pin names not known; wires that end beside it: r7, _7, b7
  Counter #(.width(2), .max('h1)) counter_1 (
    .Q(counter_1_q), .clk(CONFIRM_out));  // open: load, D, count, carry, clr, preset, down
  Button CONFIRM (.out(CONFIRM_out));
  Adder #(.width(2)) adder_1 (.a(2'b01), .b(counter_1_q), .out(adder_1_out));  // open: cin, cout
  // RGBLed rgbled_4: pin names not known; wires that end beside it: r2, _2, b2
  // RGBLed rgbled_5: pin names not known; wires that end beside it: r5, _5, b5
  // RGBLed rgbled_6: pin names not known; wires that end beside it: r8, _8, b8
  Counter #(.width(4), .max('h8)) counter_2 (
    .Q(counter_2_q), .clk(clk));  // open: load, D, count, carry, clr, preset, down
  Button SCORRI (.out(clk));
  // RGBLed rgbled_7: pin names not known; wires that end beside it: r3, _3, b3
  // RGBLed rgbled_8: pin names not known; wires that end beside it: r6, _6, b6
  // RGBLed rgbled_9: pin names not known; wires that end beside it: r9, _9, b9
  RAM #(.addrWidth(4), .dataWidth(2), .bus("separate"), .Select("low")) ram_1 (
    .addr(counter_2_q), .din(adder_1_out), .data(ram_1_data), .clk(CONFIRM_out));  // open: str, sel, ld, clr
  Demultiplexer #(.select(4), .width(2), .enable("false")) demultiplexer_1 (
    .out0(demultiplexer_1_out0), .out1(demultiplexer_1_out1), .out2(demultiplexer_1_out2),
    .out3(demultiplexer_1_out3), .out4(demultiplexer_1_out4), .out5(demultiplexer_1_out5),
    .out6(demultiplexer_1_out6), .out7(demultiplexer_1_out7), .out8(demultiplexer_1_out8), .in(ram_1_data),
    .sel(counter_2_q));  // open: out9, out10, out11, out12, out13, out14, out15
  Register #(.width(2), .trigger("falling"), .Select("low")) register_1 (
    .D(demultiplexer_1_out0), .en(_1), .Q({b1, r1}), .clk(clk));  // open: clr
  Decoder #(.select(4), .enable("false")) decoder_1 (
    .out0(_1), .out1(_2), .out2(_3), .out3(_4), .out4(_5), .out5(_6), .out6(_7), .out7(_8), .out8(_9),
    .sel(counter_2_q));  // open: out9, out10, out11, out12, out13, out14, out15
  Register #(.width(2), .trigger("falling"), .Select("low")) register_2 (
    .D(demultiplexer_1_out2), .en(_3), .Q({b3, r3}), .clk(clk));  // open: clr
  Register #(.width(2), .trigger("falling"), .Select("low")) register_3 (
    .D(demultiplexer_1_out4), .en(_5), .Q({b5, r5}), .clk(clk));  // open: clr
  Register #(.width(2), .trigger("falling"), .Select("low")) register_4 (
    .D(demultiplexer_1_out1), .en(_2), .Q({b2, r2}), .clk(clk));  // open: clr
  Register #(.width(2), .trigger("falling"), .Select("low")) register_5 (
    .D(demultiplexer_1_out6), .en(_7), .Q({b7, r7}), .clk(clk));  // open: clr
  Register #(.width(2), .trigger("falling"), .Select("low")) register_6 (
    .D(demultiplexer_1_out8), .en(_9), .Q({b9, r9}), .clk(clk));  // open: clr
  Register #(.width(2), .trigger("falling"), .Select("low")) register_7 (
    .D(demultiplexer_1_out3), .en(_4), .Q({b4, r4}), .clk(clk));  // open: clr
  Register #(.width(2), .trigger("falling"), .Select("low")) register_8 (
    .D(demultiplexer_1_out5), .en(_6), .Q({b6, r6}), .clk(clk));  // open: clr
  Register #(.width(2), .trigger("falling"), .Select("low")) register_9 (
    .D(demultiplexer_1_out7), .en(_8), .Q({b8, r8}), .clk(clk));  // open: clr
endmodule
